// Digital circuit 8BitProzessor MitRam.dig as structural Verilog
module _8BitProzessor_MitRam (
  input  [23:0] DataBus_in,
  input  RDY,
  input  Clock_M,
  input  Clock_A,
  input  Enable,
  input  Enable_2,
  output [23:0] DataBus_out,
  output [23:0] AddBus,
  output WR,
  output RD,
  output [7:0] IterationPoint,
  output [23:0] A,
  output [23:0] B,
  output [23:0] Y,
  output [23:0] R_1,
  output [23:0] IP,
  output [23:0] IR,
  output [23:0] MAR,
  output [23:0] MDR,
  output [23:0] R_2,
  output [23:0] R_3,
  output [23:0] R_0,
  output [23:0] Akk,
  output [7:0] IterationPoint_2,
  output [23:0] A_2,
  output [23:0] B_2,
  output [23:0] Y_2,
  output [23:0] R_5,
  output [23:0] IP_2,
  output [7:0] IR_2,
  output [23:0] MAR_2,
  output [23:0] MDR_2,
  output [23:0] R_6,
  output [23:0] R_7,
  output [23:0] R_4,
  output [23:0] Akk_2,
  output [23:0] Bus
);

  wire _24bitin1bit_1_out, ALU_p1, ALU_p5, ALU_p6, ALU_p7, and_1_out, controlunit_1_p1, controlunit_1_p2,
       controlunit_1_p3, controlunit_1_p5, controlunit_1_p6, controlunit_1_p7, controlunit_1_p8,
       controlunit_1_p9, controlunit_1_p10, controlunit_1_p12, controlunit_1_p13, controlunit_1_p14,
       controlunit_1_p15, controlunit_1_p16, controlunit_1_p21, controlunit_1_p25, not_1_out;
  wire [1:0] controlunit_1_p11;
  wire [23:0] ALU_p3, demultiplexer_1_out_0, demultiplexer_1_out_1, demultiplexer_1_out_2,
       demultiplexer_1_out_3, driver_7_out, multiplexer_1_out, multiplexer_2_out, or_1_out, ramasync_1_q;

  Multiplexer #(.Bits(24)) multiplexer_1 (.sel(Enable_2), .in_0({24{1'b0}}), .in_1(24'h10000), .out(multiplexer_1_out));
  assign Bus = controlunit_1_p2 ? DataBus_out : 24'bz;  // Driver driver_1
  assign Bus = controlunit_1_p6 ? IR : 24'bz;  // Driver driver_2
  assign Bus = controlunit_1_p8 ? IP : 24'bz;  // Driver driver_3
  assign Bus = controlunit_1_p10 ? multiplexer_2_out : 24'bz;  // Driver driver_4
  assign Bus = controlunit_1_p13 ? Y : 24'bz;  // Driver driver_5
  assign Bus = controlunit_1_p16 ? Akk : 24'bz;  // Driver driver_6
  Demultiplexer #(.Selector_Bits(2), .Bits(24)) demultiplexer_1 (
    .sel(controlunit_1_p11), .in(Bus), .out_0(demultiplexer_1_out_0), .out_1(demultiplexer_1_out_1),
    .out_2(demultiplexer_1_out_2), .out_3(demultiplexer_1_out_3));
  assign or_1_out = driver_7_out | multiplexer_1_out | DataBus_in;  // Or or_1, 24 bits wide
  _24_BitRegister u_MDR (.I(or_1_out), .W(controlunit_1_p1), .R(1'b1), .O(DataBus_out));
  _24_BitRegister u_MAR (.I(Bus), .W(controlunit_1_p3), .R(1'b1), .O(AddBus));
  _24_BitRegister IR_InstructionRegister (.I(Bus), .W(controlunit_1_p5), .R(1'b1), .O(IR));
  _24_BitRegister IP_InstructionPointer (.I(Bus), .W(controlunit_1_p7), .R(1'b1), .O(IP));
  _24_BitRegister u_Y (.I(Bus), .W(controlunit_1_p12), .R(1'b1), .O(Y));
  _24_BitRegister _24_bitregister_1 (.I(ALU_p3), .W(controlunit_1_p15), .R(1'b1), .O(Akk));
  _24_BitRegister u_A (.I(Bus), .W(controlunit_1_p15), .R(1'b1), .O(A));
  // _24BitALU ALU: pin names not known; wires that end beside it: ALU_p1, A, ALU_p3, B, ALU_p5, ALU_p6, ALU_p7
  _24_BitRegister u_R_0 (.I(demultiplexer_1_out_0), .W(controlunit_1_p9), .R(1'b1), .O(R_3));
  _24_BitRegister u_R_1 (.I(demultiplexer_1_out_1), .W(controlunit_1_p9), .R(1'b1), .O(R_2));
  _24_BitRegister u_R_2 (.I(demultiplexer_1_out_2), .W(controlunit_1_p9), .R(1'b1), .O(R_1));
  _24_BitRegister u_R_3 (.I(demultiplexer_1_out_3), .W(controlunit_1_p9), .R(1'b1), .O(R_0));
  _24_BitRegister u_B (.I(Bus), .W(controlunit_1_p14), .R(1'b1), .O(B));
  RAMAsync #(.AddrBits(8), .Bits(24), .isProgramMemory("true")) ramasync_1 (
    .A(AddBus[7:0]), .D(DataBus_out), .we(WR), .Q(ramasync_1_q));
  _24BitIn1Bit _24bitin1bit_1 (.in(ramasync_1_q), .out(_24bitin1bit_1_out));
  not not_1 (not_1_out, _24bitin1bit_1_out);
  Multiplexer #(.Selector_Bits(2), .Bits(24)) multiplexer_2 (
    .sel(controlunit_1_p11), .in_0(R_3), .in_1(R_2), .in_2(R_1), .in_3(R_0), .out(multiplexer_2_out));
  assign driver_7_out = RD ? ramasync_1_q : 24'bz;  // Driver driver_7
  // ControlUnit controlunit_1: pin names not known; wires that end beside it: controlunit_1_p1, controlunit_1_p2, controlunit_1_p3, IR, controlunit_1_p5, controlunit_1_p6, controlunit_1_p7, controlunit_1_p8, controlunit_1_p9, controlunit_1_p10, controlunit_1_p11, controlunit_1_p12, controlunit_1_p13, controlunit_1_p14, controlunit_1_p15, controlunit_1_p16, ALU_p1, ALU_p5, ALU_p6, ALU_p7, controlunit_1_p21, IterationPoint, WR, RD, controlunit_1_p25
  or or_2 (controlunit_1_p25, RDY, not_1_out);
  and and_1 (and_1_out, Clock_A, Enable);
  or or_3 (controlunit_1_p21, Clock_M, and_1_out);

  assign A_2 = A;
  assign Akk_2 = Akk;
  assign B_2 = B;
  assign IP_2 = IP;
  assign IR_2 = IR[23:16];
  assign IterationPoint_2 = IterationPoint;
  assign MAR = AddBus;
  assign MAR_2 = AddBus;
  assign MDR = DataBus_out;
  assign MDR_2 = DataBus_out;
  assign R_4 = R_0;
  assign R_5 = R_1;
  assign R_6 = R_2;
  assign R_7 = R_3;
  assign Y_2 = Y;

  // Notes on the sheet:
  //   CPU
endmodule
