// Digital circuit 8BitProzessor.dig as structural Verilog
module _8BitProzessor (
  input  [23:0] DataBus_in,
  input  RDY,
  input  Clock_M,
  input  Clock_A,
  output [23:0] DataBus_out,
  output [23:0] AddBus,
  output WR,
  output RD,
  output [7:0] IterationPoint,
  output [23:0] A,
  output [23:0] B,
  output [23:0] Y,
  output [23:0] R_1,
  output [23:0] IP,
  output [23:0] IR,
  output [23:0] MAR,
  output [23:0] MDR,
  output [23:0] R_2,
  output [23:0] R_3,
  output [23:0] R_0,
  output [23:0] Akk
);

  wire ALU_p1, ALU_p5, ALU_p6, ALU_p7, controlunit_1_p1, controlunit_1_p2, controlunit_1_p3,
       controlunit_1_p5, controlunit_1_p6, controlunit_1_p7, controlunit_1_p8, controlunit_1_p9,
       controlunit_1_p10, controlunit_1_p12, controlunit_1_p13, controlunit_1_p14, controlunit_1_p15,
       controlunit_1_p16, controlunit_1_p21;
  wire [1:0] controlunit_1_p11;
  wire [23:0] ALU_p3, demultiplexer_1_out_0, demultiplexer_1_out_1, demultiplexer_1_out_2,
       demultiplexer_1_out_3, driver_1_out, multiplexer_1_out, or_1_out;

  assign driver_1_out = controlunit_1_p2 ? DataBus_out : 24'bz;  // Driver driver_1
  assign driver_1_out = controlunit_1_p6 ? IR : 24'bz;  // Driver driver_2
  assign driver_1_out = controlunit_1_p8 ? IP : 24'bz;  // Driver driver_3
  assign driver_1_out = controlunit_1_p10 ? multiplexer_1_out : 24'bz;  // Driver driver_4
  assign driver_1_out = controlunit_1_p13 ? Y : 24'bz;  // Driver driver_5
  assign driver_1_out = controlunit_1_p16 ? Akk : 24'bz;  // Driver driver_6
  Demultiplexer #(.Selector_Bits(2), .Bits(24)) demultiplexer_1 (
    .sel(controlunit_1_p11), .in(driver_1_out), .out_0(demultiplexer_1_out_0), .out_1(demultiplexer_1_out_1),
    .out_2(demultiplexer_1_out_2), .out_3(demultiplexer_1_out_3));
  assign or_1_out = DataBus_in | driver_1_out;  // Or or_1, 24 bits wide
  _24_BitRegister u_MDR (.I(or_1_out), .W(controlunit_1_p1), .R(1'b1), .O(DataBus_out));
  _24_BitRegister u_MAR (.I(driver_1_out), .W(controlunit_1_p3), .R(1'b1), .O(AddBus));
  _24_BitRegister IR_InstructionRegister (.I(driver_1_out), .W(controlunit_1_p5), .R(1'b1), .O(IR));
  _24_BitRegister IP_InstructionPointer (.I(driver_1_out), .W(controlunit_1_p7), .R(1'b1), .O(IP));
  _24_BitRegister u_Y (.I(driver_1_out), .W(controlunit_1_p12), .R(1'b1), .O(Y));
  _24_BitRegister _24_bitregister_1 (.I(ALU_p3), .W(controlunit_1_p15), .R(1'b1), .O(Akk));
  _24_BitRegister u_A (.I(driver_1_out), .W(controlunit_1_p15), .R(1'b1), .O(A));
  // _24BitALU ALU: pin names not known; wires that end beside it: ALU_p1, A, ALU_p3, B, ALU_p5, ALU_p6, ALU_p7
  _24_BitRegister u_R_0 (.I(demultiplexer_1_out_0), .W(controlunit_1_p9), .R(1'b1), .O(R_3));
  _24_BitRegister u_R_1 (.I(demultiplexer_1_out_1), .W(controlunit_1_p9), .R(1'b1), .O(R_2));
  _24_BitRegister u_R_2 (.I(demultiplexer_1_out_2), .W(controlunit_1_p9), .R(1'b1), .O(R_1));
  _24_BitRegister u_R_3 (.I(demultiplexer_1_out_3), .W(controlunit_1_p9), .R(1'b1), .O(R_0));
  _24_BitRegister u_B (.I(driver_1_out), .W(controlunit_1_p14), .R(1'b1), .O(B));
  Multiplexer #(.Selector_Bits(2), .Bits(24)) multiplexer_1 (
    .sel(controlunit_1_p11), .in_0(R_3), .in_1(R_2), .in_2(R_1), .in_3(R_0), .out(multiplexer_1_out));
  // ControlUnit controlunit_1: pin names not known; wires that end beside it: controlunit_1_p1, controlunit_1_p2, controlunit_1_p3, IR, controlunit_1_p5, controlunit_1_p6, controlunit_1_p7, controlunit_1_p8, controlunit_1_p9, controlunit_1_p10, controlunit_1_p11, controlunit_1_p12, controlunit_1_p13, controlunit_1_p14, controlunit_1_p15, controlunit_1_p16, ALU_p1, ALU_p5, ALU_p6, ALU_p7, controlunit_1_p21, IterationPoint, WR, RD, 1'b1
  or or_2 (controlunit_1_p21, Clock_M, Clock_A);

  assign MAR = AddBus;
  assign MDR = DataBus_out;

  // Notes on the sheet:
  //   CPU
endmodule
