// Digital circuit ControlUnit.dig as structural Verilog
module ControlUnit (
  input  [23:0] Decodierung,
  input  Ca,
  input  _0,
  input  in_21,
  input  RDY,
  input  clock,
  output MDR_inSplit,
  output MDR_outOP,
  output MAR_in,
  output WR,
  output RD,
  output IR_in,
  output IR_op_out,
  output IP_in,
  output IP_out,
  output R_in,
  output R_out,
  output [1:0] SR_eq_ROPx,
  output B_in,
  output Y_in,
  output Y_out,
  output A_in,
  output ALU_out,
  output [3:0] F_eq_x,
  output [7:0] IterationPoint,
  output MDR_outA1,
  output MDR_outA0,
  output MDR_out,
  output MDR_inBus
);

  wire _8bitin1bit_1_out, _8bitin1bit_2_out, _8bitin1bit_3_out, and_1_out, and_2_out, delay_1_out,
       kombinatorischeschaltung_1_p4, kombinatorischeschaltung_1_p5, kombinatorischeschaltung_1_p26,
       multiplexer_2_out, multiplexer_3_out, multiplexer_4_out, or_1_out, or_2_out, undriven, undriven_2,
       undriven_3;
  wire [1:0] kombinatorischeschaltung_1_p27;
  wire [7:0] kombinatorischeschaltung_1_p30, multiplexer_1_out;

  Multiplexer #(.Bits(8)) multiplexer_1 (
    .sel(undriven_3), .in_0(kombinatorischeschaltung_1_p30), .in_1(Decodierung[7:0]), .out(multiplexer_1_out));
  _8BitIn1Bit _8bitin1bit_1 (.in(Decodierung[7:0]), .out(_8bitin1bit_1_out));
  and and_1 (and_1_out, RDY, clock);
  Multiplexer multiplexer_2 (.sel(delay_1_out), .in_0(clock), .in_1(and_1_out), .out(multiplexer_2_out));
  and and_2 (and_2_out, ~_8bitin1bit_1_out, undriven_3);  // And
  // KombinatorischeSchaltung kombinatorischeschaltung_1: pin names not known; wires that end beside it: MDR_inBus, MDR_inSplit, MDR_out, kombinatorischeschaltung_1_p4, kombinatorischeschaltung_1_p5, MDR_outA0, MDR_outA1, MDR_outOP, MAR_in, IR_in, IR_op_out, IP_in, IP_out, R_in, R_out, SR_eq_ROPx, IterationPoint, Y_in, Y_out, B_in, A_in, ALU_out, F_eq_x, kombinatorischeschaltung_1_p4, kombinatorischeschaltung_1_p5, kombinatorischeschaltung_1_p26, kombinatorischeschaltung_1_p27, RD, WR, kombinatorischeschaltung_1_p30
  Multiplexer multiplexer_3 (.sel(and_2_out), .in_0(or_2_out), .in_1(1'b1), .out(multiplexer_3_out));
  Delay delay_1 (.in(undriven_2), .out(delay_1_out));
  _8BitIn1Bit _8bitin1bit_2 (.in(kombinatorischeschaltung_1_p30), .out(_8bitin1bit_2_out));
  _8BitIn1Bit _8bitin1bit_3 (.in(multiplexer_1_out), .out(_8bitin1bit_3_out));
  or or_1 (or_1_out, _8bitin1bit_2_out, _8bitin1bit_3_out);
  or or_2 (or_2_out, undriven, multiplexer_4_out);
  CounterPreset #(.Bits(8)) \Sequenzzähler  (
    .en(1'b1), .C(multiplexer_2_out), .dir(1'b0), .in(multiplexer_1_out), .ld(or_1_out),
    .clr(multiplexer_3_out), .out(IterationPoint));  // open: ovf
  Multiplexer #(.Selector_Bits(2)) multiplexer_4 (
    .sel(kombinatorischeschaltung_1_p27), .in_0(1'b0), .in_1(Ca), .in_2(_0), .in_3(in_21),
    .out(multiplexer_4_out));
endmodule
